// Digital circuit RV5-PROCESSOR.dig as structural Verilog
module RV5_PROCESSOR (
  input  clock,
  input  in_3,
  input  in_8,
  input  in_9,
  input  in_10,
  input  clk,
  output [6:0] opcode,
  output out_4,
  output [1:0] out_5,
  output out_6,
  output [31:0] out_7,
  output out_12,
  output out_13
);

  wire abstractcs_wen, alu_mod, and_1_out, and_2_out, and_3_out, and_4_out, and_5_out, and_6_out, and_7_out,
       and_8_out, and_9_out, and_10_out, and_12_out, and_13_out, and_14_out, br_cond, branch_sel, clk_t,
       command_reg_aarpostincrement, command_reg_postexec, command_reg_transfer, command_reg_write,
       command_wen, comparator_1_eq, comparator_2_eq, comparator_3_eq, comparator_4_gt, comparator_5_lt,
       csr_opclear, csr_opset, csr_opwrite, csr_useimm, csr_wen, d_ff_1_q, d_ff_3_q, d_ff_4_q, d_ff_5_q,
       d_ff_6_q, detrs_1_o, dmcontrol_ackhavereset, dmcontrol_clrresethaltreq, dmcontrol_resumereq,
       dmcontrol_setresethaltreq, dmcontrol_wen, dmi_ack_q, dmi_ren, dmi_req, dmi_wen, dmstatus_wen,
       dret_sel, ebreak_sel, ecall_sel, GDB_p3, GDB_p5, GDB_p6, GDB_p7, haltreq, I_imm_sel, jal_sel,
       jalr_sel, ld_signext, mret_sel, multiplexer_6_out, not_1_out, not_2_out, not_3_out, not_4_out,
       not_5_out, not_6_out, not_7_out, or_1_out, or_2_out, or_3_out, or_6_out, or_8_out, or_9_out, ram_b,
       ram_h, ram_ren, ram_wen, reg_wen, S_imm_sel, SB_imm_sel, stopcond, U_imm_sel, UJ_imm_sel;
  wire [1:0] alu_a_sel, wb_sel;
  wire [1:1] rv5_tap_1_dmi_op;
  wire [2:0] alu_op, command_reg_aarsize, funct3;
  wire [3:0] dmi_addr_lut_out;
  wire [4:0] multiplexer_12_out, multiplexer_13_out, rd, rs1, rs2;
  wire [6:0] funct7, rv5_tap_1_dmi_addr;
  wire [9:8] dmstatus_q;
  wire [11:0] system_imm;
  wire [15:0] command_reg_regno;
  wire [28:24] abstractcs_q;
  wire [31:0] abstractcs, addr_dm, and_15_out, command, csr_out, dcsr, dmcontrol, dmi_rdata, dmstatus, dpc,
       imm_32, mepc, mtvec, multiplexer_1_out, multiplexer_7_out, multiplexer_8_out, multiplexer_10_out,
       multiplexer_11_out, multiplexer_14_out, multiplexer_15_out, not_8_out, or_7_out, out_dm, ra,
       rv5_alu_1_y, rv5_gpr_1_rb, rv5_memory_1_out, rv5_memory_1_out_inst, rv5_pcu_1_pc;
  wire [31:2] add_1_s;
  wire [31:23] multiplexer_3_out;

  and and_1 (and_1_out, dmcontrol_wen, out_7[2]);
  and and_2 (and_2_out, dmcontrol_wen, out_7[3]);
  and and_3 (and_3_out, dmcontrol_wen, out_7[28]);
  and and_4 (and_4_out, dmcontrol_wen, out_7[30]);
  or or_1 (or_1_out, clk_t, clk_t);
  and and_5 (and_5_out, not_1_out, clk_t);
  not not_1 (not_1_out, clk_t);
  and and_6 (and_6_out, not_2_out, clk_t);
  not not_2 (not_2_out, clk_t);
  and and_7 (and_7_out, not_3_out, clk_t);
  not not_3 (not_3_out, clk_t);
  and and_8 (and_8_out, not_4_out, or_1_out);
  not not_4 (not_4_out, clk_t);
  D_FF_AS d_ff_as_1 (.Set(1'b0), .D(and_1_out), .C(clk_t), .Clr(and_5_out), .Q(dmcontrol_clrresethaltreq));  // open: nQ
  D_FF_AS d_ff_as_2 (.Set(1'b0), .D(and_2_out), .C(clk_t), .Clr(and_6_out), .Q(dmcontrol_setresethaltreq));  // open: nQ
  D_FF_AS d_ff_as_3 (.Set(1'b0), .D(and_3_out), .C(clk_t), .Clr(and_7_out), .Q(dmcontrol_ackhavereset));  // open: nQ
  D_FF_AS d_ff_as_4 (.Set(1'b0), .D(and_4_out), .C(clk_t), .Clr(and_8_out), .Q(dmcontrol_resumereq));  // open: nQ
  RS_FF_AS rs_ff_as_1 (.S(and_8_out), .R(1'b0), .Q(out_13));  // open: nQ
  and and_9 (and_9_out, clk_t, command_wen);
  Register #(.Bits(32)) u_dmcontrol (
    .D({out_7[31], {5{1'b0}}, out_7[25:6], 4'b0000, out_7[1:0]}), .C(clk_t), .en(dmcontrol_wen), .Q(dmcontrol));
  Register #(.Bits(32)) u_dmstatus (
    .D(out_7), .C(clk_t), .en(dmstatus_wen), .Q({dmstatus[31:10], dmstatus_q, dmstatus[7:0]}));
  Register #(.Bits(32)) u_abstractcs (
    .D(out_7), .C(clk_t), .en(abstractcs_wen), .Q({abstractcs[31:29], abstractcs_q, abstractcs[23:0]}));
  Multiplexer #(.Bits(32)) multiplexer_1 (.sel(and_9_out), .in_0({32{1'b0}}), .in_1(out_7), .out(multiplexer_1_out));
  detrs detrs_1 (.set(and_9_out), .reset(clk_t), .O(detrs_1_o));
  Register dmi_ack (.D(dmi_req), .C(clk_t), .en(1'b1), .Q(dmi_ack_q));
  Register register_1 (.D(dmcontrol_resumereq), .C(clk_t), .en(dmcontrol_resumereq), .Q(out_12));
  not not_5 (not_5_out, detrs_1_o);
  and and_10 (and_10_out, and_9_out, not_5_out);
  // Gdb GDB: pin names not known; wires that end beside it: clk, clk_t, GDB_p3, clk_t, GDB_p5, GDB_p6, GDB_p7
  D_FF d_ff_1 (.D(dmi_req), .C(clk_t), .Q(d_ff_1_q));  // open: nQ
  D_FF #(.Bits(32)) d_ff_2 (.D(multiplexer_1_out), .C(and_10_out));  // open: Q, nQ
  Multiplexer #(.Bits(32)) multiplexer_2 (.sel(command_wen), .in_0({32{1'b0}}), .in_1(out_7), .out(command));
  or or_2 (or_2_out, dmi_req, d_ff_1_q);
  RV5_TAP rv5_tap_1 (
    .TCK(GDB_p5), .RESET(in_3), .TDI(GDB_p7), .TMS(GDB_p6), .DMI_ACK(dmi_ack_q), .DMI_RDATA(dmi_rdata),
    .DMI_STATUS(2'b00), .TDO(GDB_p3), .DMI_REQ(dmi_req), .DMI_ADDR(rv5_tap_1_dmi_addr), .DMI_WDATA(out_7),
    .DMI_OP({rv5_tap_1_dmi_op[1], dmi_ren}), .E_DMI_BUSY(out_4), .E_STICKY_ERR(out_5));  // open: E_DMISTAT
  not not_6 (not_6_out, abstractcs[12]);
  and and_11 (dmi_wen, dmi_req, not_6_out, rv5_tap_1_dmi_op[1]);
  LookUpTable #(.Bits(4)) dmi_addr_lut (
    .in0(rv5_tap_1_dmi_addr[0]), .in1(rv5_tap_1_dmi_addr[1]), .in2(rv5_tap_1_dmi_addr[2]),
    .in3(rv5_tap_1_dmi_addr[3]), .in4(rv5_tap_1_dmi_addr[4]), .in5(rv5_tap_1_dmi_addr[5]),
    .in6(rv5_tap_1_dmi_addr[6]), .out(dmi_addr_lut_out));
  Comparator #(.Bits(8)) comparator_1 (.a(command[31:24]), .b({8{1'b0}}), .eq(comparator_1_eq));  // open: gt, lt
  Multiplexer #(.Bits(32)) multiplexer_3 (
    .sel(comparator_1_eq), .in_0({32{1'b0}}), .in_1(command),
    .out({multiplexer_3_out, command_reg_aarsize, command_reg_aarpostincrement, command_reg_postexec, command_reg_transfer, command_reg_write, command_reg_regno}));
  Demultiplexer #(.Selector_Bits(4)) demultiplexer_1 (
    .sel(dmi_addr_lut_out), .in(dmi_wen), .out_2(dmcontrol_wen), .out_3(dmstatus_wen),
    .out_5(abstractcs_wen), .out_6(command_wen));  // open: out_0, out_1, out_4, out_7, out_8, out_9, out_10, out_11, out_12, out_13, out_14, out_15
  and and_12 (and_12_out, dmcontrol_resumereq, dcsr[2]);
  Multiplexer #(.Selector_Bits(4), .Bits(32)) multiplexer_4 (
    .sel(dmi_addr_lut_out), .in_0({32{1'b0}}), .in_1(out_dm), .in_2(dmcontrol),
    .in_3({dmstatus[31:9], dmstatus[9], dmstatus[7:0]}), .in_4(32'h100001),
    .in_5({abstractcs[31:29], 5'b00100, abstractcs[23:0]}), .in_6(command), .in_7(out_dm), .in_8(out_dm),
    .in_9(out_dm), .in_10(out_dm), .in_11(out_dm), .in_12(out_dm), .in_13(out_dm), .in_14(out_dm),
    .in_15({32{1'b0}}), .out(dmi_rdata));
  D_FF d_ff_3 (.D(and_12_out), .C(clk_t), .Q(d_ff_3_q));  // open: nQ
  D_FF d_ff_4 (.D(in_10), .C(clk_t), .Q(d_ff_4_q));  // open: nQ
  Comparator #(.Bits(32)) comparator_2 (.a(rv5_pcu_1_pc), .b(32'h190), .eq(comparator_2_eq));  // open: gt, lt
  Comparator #(.Bits(32)) comparator_3 (.a(rv5_pcu_1_pc), .b(32'h194), .eq(comparator_3_eq));  // open: gt, lt
  Comparator #(.Bits(32)) comparator_4 (.a(rv5_pcu_1_pc), .b(32'h1003), .gt(comparator_4_gt));  // open: eq, lt
  Comparator #(.Bits(32)) comparator_5 (.a(rv5_pcu_1_pc), .b(32'h1021), .lt(comparator_5_lt));  // open: gt, eq
  not not_7 (not_7_out, d_ff_4_q);
  or or_3 (or_3_out, comparator_2_eq, comparator_3_eq);
  D_FF d_ff_5 (.D(d_ff_3_q), .C(clk_t), .Q(d_ff_5_q));  // open: nQ
  and and_13 (and_13_out, not_7_out, in_10);
  Multiplexer #(.Selector_Bits(4), .Bits(32)) multiplexer_5 (
    .sel(dmi_addr_lut_out), .in_0({32{1'b0}}), .in_1(32'h1024), .in_2({32{1'b0}}), .in_3({32{1'b0}}),
    .in_4({32{1'b0}}), .in_5({32{1'b0}}), .in_6({32{1'b0}}), .in_7(32'h1004), .in_8(32'h1008),
    .in_9(32'h100c), .in_10(32'h1010), .in_11(32'h1014), .in_12(32'h1018), .in_13(32'h101c),
    .in_14(32'h1020), .in_15({32{1'b0}}), .out(addr_dm));
  or or_4 (dmstatus[9], or_3_out, and_14_out);
  and and_14 (and_14_out, comparator_4_gt, comparator_5_lt);
  D_FF d_ff_6 (.D(d_ff_5_q), .C(clk_t), .Q(d_ff_6_q));  // open: nQ
  or or_5 (haltreq, dmcontrol[31], d_ff_6_q);
  Multiplexer multiplexer_6 (.sel(in_10), .in_0(1'b0), .in_1(1'b0), .out(multiplexer_6_out));
  or or_6 (or_6_out, 1'b0, and_13_out);
  Register register_2 (.D(and_14_out), .C(clk_t), .en(and_14_out), .Q(out_6));
  Register register_3 (.D(multiplexer_6_out), .C(clk_t), .en(or_6_out), .Q(stopcond));
  Multiplexer #(.Bits(32)) multiplexer_7 (
    .sel(csr_useimm), .in_0(ra), .in_1({{27{1'b0}}, rs1}), .out(multiplexer_7_out));
  assign not_8_out = ~multiplexer_7_out;  // Not not_8, 32 bits wide
  assign and_15_out = not_8_out & csr_out;  // And and_15, 32 bits wide
  assign or_7_out = multiplexer_7_out | csr_out;  // Or or_7, 32 bits wide
  Multiplexer #(.Bits(32)) multiplexer_8 (
    .sel(csr_opclear), .in_0(multiplexer_7_out), .in_1(and_15_out), .out(multiplexer_8_out));
  Multiplexer multiplexer_9 (.sel(or_8_out), .in_0(clock), .in_1(in_8), .out(clk_t));
  RV5_PCU rv5_pcu_1 (
    .IMM_32(imm_32), .CLK(clk_t), .IS_BRANCH(branch_sel), .IS_JAL(jal_sel), .IS_JALR(jalr_sel),
    .COND_MET(br_cond), .ALU_OUT(rv5_alu_1_y), .IS_ECALL(ecall_sel), .MTVEC(mtvec), .MEPC(mepc),
    .IS_MRET(mret_sel), .IS_EBREAK(ebreak_sel), .IS_DEBUG(dmstatus[9]), .DCSR(dcsr), .DPC(dpc),
    .IS_DRET(dret_sel), .HALTREQ(haltreq), .POSTEXEC(command_reg_postexec), .RESUMEREQ(dmcontrol_resumereq),
    .PC(rv5_pcu_1_pc));
  Multiplexer #(.Bits(32)) multiplexer_10 (
    .sel(csr_opset), .in_0(multiplexer_8_out), .in_1(or_7_out), .out(multiplexer_10_out));
  or or_8 (or_8_out, in_9, stopcond);
  RV5_IMM rv5_imm_1 (
    .UJ_imm_sel(UJ_imm_sel), .I_imm_sel(I_imm_sel), .SB_imm_sel(SB_imm_sel), .S_imm_sel(S_imm_sel),
    .U_imm_sel(U_imm_sel), .INSTR_32(rv5_memory_1_out_inst), .imm(imm_32));
  Add #(.Bits(30)) add_1 (.a(rv5_pcu_1_pc[31:2]), .b({30{1'b0}}), .c_i(1'b1), .s(add_1_s));  // open: c_o
  RV5_CSR rv5_csr_1 (
    .clk(clk_t), .addr(system_imm), .w_data(multiplexer_10_out), .wen(csr_wen), .pc_in(rv5_pcu_1_pc),
    .ecall_sel(ecall_sel), .mret_sel(mret_sel), .ebreak_sel(ebreak_sel), .is_debug(dmstatus[9]),
    .haltreq(haltreq), .R_DATA(csr_out), .MTVEC_OUT(mtvec), .MEPC_OUT(mepc), .DCSR_OUT(dcsr), .DPC_OUT(dpc));
  RV5_INSTR_DECODE rv5_instr_decode_1 (
    .instr(rv5_memory_1_out_inst), .funct7(funct7), .rs2(rs2), .rs1(rs1), .funct3(funct3), .rd(rd),
    .opcode(opcode), .UJ_imm_sel(UJ_imm_sel), .U_imm_sel(U_imm_sel), .S_imm_sel(S_imm_sel),
    .SB_imm_sel(SB_imm_sel), .I_imm_sel(I_imm_sel), .alu_mod(alu_mod), .ram_wen(ram_wen), .wb_sel(wb_sel),
    .ram_ren(ram_ren), .ecall_sel(ecall_sel), .alu_op(alu_op), .ram_b(ram_b), .ram_h(ram_h),
    .reg_wen(reg_wen), .branch_sel(branch_sel), .jal_sel(jal_sel), .jalr_sel(jalr_sel),
    .alu_a_sel(alu_a_sel), .ld_signext(ld_signext), .csr_wen(csr_wen), .mret_sel(mret_sel),
    .system_imm(system_imm), .ebreak_sel(ebreak_sel), .dret_sel(dret_sel), .csr_opwrite(csr_opwrite),
    .csr_opset(csr_opset), .csr_opclear(csr_opclear), .csr_useimm(csr_useimm));
  Multiplexer #(.Selector_Bits(2), .Bits(32)) multiplexer_11 (
    .sel(wb_sel), .in_0(rv5_alu_1_y), .in_1({add_1_s, 2'b00}), .in_2(rv5_memory_1_out), .in_3(csr_out),
    .out(multiplexer_11_out));
  Multiplexer #(.Bits(5)) multiplexer_12 (.sel(ecall_sel), .in_0(rs1), .in_1(5'b01010), .out(multiplexer_12_out));
  Multiplexer #(.Bits(5)) multiplexer_13 (.sel(ecall_sel), .in_0(rs2), .in_1(5'b10001), .out(multiplexer_13_out));
  RV5_GPR rv5_gpr_1 (
    .RS1(multiplexer_12_out), .RS2(multiplexer_13_out), .D_in(multiplexer_11_out), .clk(clk_t),
    .WEN(reg_wen), .RD(rd), .RA(ra), .RB(rv5_gpr_1_rb));  // open: RD0
  RV5_MEMORY rv5_memory_1 (
    .addr(rv5_alu_1_y), .wdata(rv5_gpr_1_rb), .wen(ram_wen), .ren(ram_ren), .clk(clk_t), .\byte (ram_b),
    .half(ram_h), .signext(ld_signext), .addr_inst(rv5_pcu_1_pc), .addr_dm(addr_dm), .wen_dm(dmi_wen),
    .wdata_dm(out_7), .out(rv5_memory_1_out), .out_inst(rv5_memory_1_out_inst), .out_dm(out_dm));
  Multiplexer #(.Selector_Bits(2), .Bits(32)) multiplexer_14 (
    .sel(alu_a_sel), .in_0(ra), .in_1(rv5_pcu_1_pc), .in_2({32{1'b0}}), .in_3({32{1'b0}}),
    .out(multiplexer_14_out));
  Multiplexer #(.Bits(32)) multiplexer_15 (
    .sel(or_9_out), .in_0(rv5_gpr_1_rb), .in_1(imm_32), .out(multiplexer_15_out));
  or or_9 (or_9_out, I_imm_sel, S_imm_sel, U_imm_sel);
  RV5_ALU rv5_alu_1 (
    .OP(alu_op), .Y(rv5_alu_1_y), .A(multiplexer_14_out), .B(multiplexer_15_out), .BR(br_cond), .MOD(alu_mod));

  // Other names for the same wires on the sheet: abstractcs_datacount[3:0] = abstractcs[3:0];
  //   abstractcs_err[2:0] = abstractcs[10:8]; abstractcs_busy = abstractcs[12]; dmstatus_allrunning = dmstatus[7];
  //   command_cmdtype[7:0] = command[31:24]; dclk = clk_t; dmcontrol_dmactive = dmcontrol[0];
  //   dmcontrol_ndmreset = dmcontrol[1]; dmcontrol_hartselhi[9:0] = dmcontrol[15:6];
  //   dmcontrol_hartsello[9:0] = dmcontrol[25:16]; dmcontrol_hasel = dmcontrol[26];
  //   dmcontrol_hartreset = dmcontrol[29]; dmcontrol_haltreq = dmcontrol[31]; dmi_wdata[31:0] = out_7;
  //   dmstatus[8] = dmstatus[9]; dmstatus_allhalted = dmstatus[9]; dmstatus_anyhalted = dmstatus[9];
  //   is_debug = dmstatus[9]

  // Notes on the sheet:
  //   clock: Hz: 2147483647
  //   in_8: default 1
  //   clk: Hz: 50000
  //   ^ WIP DEBUG STUFF
  //   We only support the access register
  //   command. This is because it 
  //   can execute arbitrary code in
  //   progbuf, allowing us to do 
  //   everything we want.
  //   contents of dmi_addr_lut (hex, n*v repeats v):
  //   4*0,1,11*0,2,3,4,0,0,0,5,6,8*0,7,8,9,a,b,c,d,e
  //   For now, address range check is
  //   the most robust way to know if
  //   we're in debug mode.
  //   Might change so debug ROM length
  //   is variable, but for now I KNOW this
  //   works.
  //   Here we are trying to make this circuit hierarchical
  //       RV5-REGS contains register bank related hw.
  //       RV5-ALU contains ALU related hw
  //       RV5-INSTR-DECODE contains Instruction Reg, and all needed decodes
  //             decoder for immediate sel
  //       RV5-IMM is a combinatorial that extracts the needed immediates, 
  //              and provides the sign-extended 32-bit value thru a MUX.
  //       RV5-PCU needs some fixes.
  //              increments the PC and allows Jumps, and provides next PC for JAL save of PC.
  //   See examples in Digital in particular processors as to how 
  //   to do this.  
  //   TODO: 
  //   1st. Add a test to each element in the hierarchy.
  //   2nd Resize boxes with appropriate SVG for readable packages w. appropriate signals.
  //   We need to:
  //       RV5-INSTR-DECODE: Decodes the instruction set and provides control signals, and FMT
  //            decode for immediate select has been completed.
  //       Implement:
  //            RV5-LOAD-STORE: Provides Load and Store
  //            RV5-MEMORY: Include ROM and RAM.
  //            RV5-IO: Provides a mean to read a program, communicate with a terminal (keyboard/display)
  //            Create a ROM/RAM  bootstrap
  //                 that loads a program.
  //   Note: Assembler test programs can be found at:   
  //      https://github.com/riscv-software-src/riscv-tests
  //   PCU (Program Control Unit, 
  //   PC = PC + 4, or PC = PC += SBimm32
  //   or PC = ALU out or PC += sgn_ext-imm32
  //   for FMT U, and UJ
  //   Need to figure out a way to load memory
  //   with instructions, ideally from RARS.
  //   Check out how MARS does it for MIPS.
  //   NEXT, NEED LOAD AND STORE,
  //   Address comes from ALU output
  //   which goes to memory via see-thru latch
  //    latch,which goes out to memory for 
  //   loading and storing.  reads 32-word
  //   and stores in rd.   Need to figure out a good
  //   approach to read and write to memory 
  //   with Digital and load it at start up.
  //   We need to arbitrate use of memory 
  //   between load/store and fetching instruction.
  //   RV5-DECODER:
  //      decodes: opcode, funct3, funct7
  //      generates: 
  //           # FMT - DO I NEED IT HERE?
  //           # imm_sel,  DONE ALREADY
  //           wen, 
  //           sub/add, 
  //           func_sel
endmodule
